# Fritzing sketch led01 (saved by Fritzing 0.9.2b)

parts:
  LED1 = LED - 5mm [color="Red (633nm)" package="5 mm [THT]"]
  Raspberry_Pi1 = Raspberry Pi 2
  R1 = Resistor [tolerance=±5% resistance=220 package=THT]

nets:
  N1: LED1.anode, Raspberry_Pi1.GPIO18
  N2: Raspberry_Pi1.GND, R1.Pin_0
